# Fritzing sketch DiscoJar (saved by Fritzing 0.9.3b)
breadboards: 1

parts:
  Teensy_3_1 = Teensy 3.1
  5V_LED_power_supply = Power plug
  R1 = Resistor [tolerance=±5% resistance=47k package=THT]
  R2 = Resistor [tolerance=±5% resistance=47k package=THT]
  C1 = Electrolytic Capacitor [capacitance=10µF package="100 mil [THT, electrolytic]"]
  C2 = Electrolytic Capacitor [capacitance=10µF package="100 mil [THT, electrolytic]"]
  R3 = Resistor [tolerance=±5% resistance=10k package=THT]
  R4 = Resistor [tolerance=±5% resistance=2.2k package=THT]
  Audio_Input = 3.5mm Audio Jack [package=audio-jack]
  U1 = ESP8266 WiFi Module [part_number=ESP8266]
  R5 = Resistor [tolerance=±5% resistance=1k package=THT]

nets:
  GND: Teensy_3_1.GND, 5V_LED_power_supply.GND, U1.GND
  N1: R1.Pin_0, C2.-, R4.Pin_0, Audio_Input.SLEEVE
  N2: R1.Pin_1, C1.-, Audio_Input.RIGHT
  N3: R2.Pin_0, C1.+
  N4: R2.Pin_1, C2.+, R3.Pin_0, R4.Pin_1
  N5: R3.Pin_1, U1.VCC, R5.Pin_0
  N6: U1.CH_PD, R5.Pin_1

notes:
  LED CLOCK
  LED GND
  LED VCC
  LED DATA IN
  connect to APA 102 strip
  AGND and 3.3V
  A2 ADC INPUT

custom parts:
  ESP8266 WiFi Module: Generic WiFi Module based on the ESP8266 with onboard PCB antenna and UART communications
